# Fritzing sketch v01 (saved by Fritzing 0.9.10b)
perfboards: 1

parts:
  U1 = ESP32-38PinWide [part_number=ESP32-38PinWide]  # not connected
  JP3 = Header 8 [package=1x08_smd]  # not connected
  JP4 = Header 1 [package=1x01_offset]  # not connected
  R1 = Resistor [tolerance=±5% resistance=10k package="0805 [SMD]"]  # not connected
  R2 = Resistor [tolerance=±5% resistance=10k package="0805 [SMD]"]  # not connected
  R3 = Resistor [tolerance=±5% resistance=10k package="0805 [SMD]"]  # not connected
  R4 = Resistor [tolerance=±5% resistance=10k package="0805 [SMD]"]  # not connected
  R5 = Resistor [tolerance=±5% resistance=10k package="0805 [SMD]"]  # not connected
  R6 = Resistor [tolerance=±5% resistance=10k package="0805 [SMD]"]  # not connected
  R7 = Resistor [tolerance=±5% resistance=10k package="0805 [SMD]"]  # not connected
  R8 = Resistor [tolerance=±5% resistance=10k package="0805 [SMD]"]  # not connected
  JP5 = Header 4 [package=jst-4-pth]

nets:
  N1: JP5.3, JP5.4

notes:
  ZNX-01 plug
  IMU (unused in v0.1)

custom parts:
  ESP32-38PinWide: Generic 38-Pin ESP32 with wide format (only access to one side of pins on a breadboard) based on Stephen Lilley's HiLetgo ESP-WROOM-32 ESP32 ESP-32S Development Board.
