# Fritzing sketch v02 (saved by Fritzing 0.9.10b)
perfboards: 2

parts:
  U1 = ESP32-38PinWide [part_number=ESP32-38PinWide]  # not connected
  JP3 = Header 8 [package=1x08_smd]  # not connected
  JP4 = Header 1 [package=1x01_offset]  # not connected
  R2 = Resistor [tolerance=±5% resistance=10k package="0805 [SMD]"]  # not connected
  R3 = Resistor [tolerance=±5% resistance=10k package="0805 [SMD]"]  # not connected
  R4 = Resistor [tolerance=±5% resistance=10k package="0805 [SMD]"]  # not connected
  R5 = Resistor [tolerance=±5% resistance=10k package="0805 [SMD]"]  # not connected
  R6 = Resistor [tolerance=±5% resistance=10k package="0805 [SMD]"]  # not connected
  R7 = Resistor [tolerance=±5% resistance=10k package="0805 [SMD]"]  # not connected
  R8 = Resistor [tolerance=±5% resistance=10k package="0805 [SMD]"]  # not connected
  JP5 = Header 4 [package=jst-4-pth]
  JP7 = Header 1 [package=1x01_offset]  # not connected
  JP8 = Header 1 [package=1x01_offset]  # not connected
  JP9 = Header 1 [package=1x01_offset]  # not connected
  JP10 = Header 1 [package=1x01_offset]  # not connected
  JP11 = Header 1 [package=1x01_offset]  # not connected
  JP12 = Header 1 [package=1x01_offset]  # not connected
  JP13 = Header 1 [package=1x01_offset]  # not connected
  JP14 = Header 1 [package=1x01_offset]  # not connected
  JP15 = Header 1 [package=1x01_offset]  # not connected
  JP16 = Header 1 [package=1x01_offset]  # not connected
  JP17 = Header 1 [package=1x01_offset]  # not connected
  JP18 = Header 1 [package=1x01_offset]  # not connected
  JP19 = Header 1 [package=1x01_offset]  # not connected
  JP20 = Header 1 [package=1x01_offset]  # not connected
  JP21 = Header 1 [package=1x01_offset]  # not connected
  R9 = Resistor [tolerance=±5% resistance=10k package="0402 [SMD]"]  # not connected
  JP22 = Header 1 [package=1x01_offset]  # not connected
  JP23 = Header 1 [package=1x01_offset]  # not connected
  JP24 = Header 1 [package=1x01_offset]  # not connected
  JP25 = Header 1 [package=1x01_offset]  # not connected
  JP26 = Header 1 [package=1x01_offset]  # not connected
  JP27 = Header 1 [package=1x01_offset]  # not connected
  JP28 = Header 1 [package=1x01_offset]  # not connected
  JP29 = Header 1 [package=1x01_offset]  # not connected
  JP30 = Header 1 [package=1x01_offset]  # not connected
  JP31 = Header 1 [package=1x01_offset]  # not connected
  JP32 = Header 1 [package=1x01_offset]  # not connected
  JP33 = Header 1 [package=1x01_offset]  # not connected

nets:
  N1: JP5.3, JP5.4

notes:
  ZNX-01 plug
  IMU (unused in v0.1)

custom parts:
  ESP32-38PinWide: Generic 38-Pin ESP32 with wide format (only access to one side of pins on a breadboard) based on Stephen Lilley's HiLetgo ESP-WROOM-32 ESP32 ESP-32S Development Board.
