# Fritzing sketch v03 (saved by Fritzing 0.9.10b)
perfboards: 2

parts:
  U1 = ESP32-38PinWide [part_number=ESP32-38PinWide]
  JP3 = Header 8 [package=1x08_smd]
  JP4 = Header 1 [package=1x01_offset]  # not connected
  R2 = Resistor [tolerance=±5% resistance=10k package="0805 [SMD]"]  # not connected
  R3 = Resistor [tolerance=±5% resistance=10k package="0805 [SMD]"]  # not connected
  R4 = Resistor [tolerance=±5% resistance=10k package="0805 [SMD]"]  # not connected
  R5 = Resistor [tolerance=±5% resistance=10k package="0805 [SMD]"]  # not connected
  R6 = Resistor [tolerance=±5% resistance=10k package="0805 [SMD]"]  # not connected
  R7 = Resistor [tolerance=±5% resistance=10k package="0805 [SMD]"]  # not connected
  R8 = Resistor [tolerance=±5% resistance=10k package="0805 [SMD]"]  # not connected
  JP7 = Header 1 [package=1x01_offset]  # not connected
  JP8 = Header 1 [package=1x01_offset]
  JP9 = Header 1 [package=1x01_offset]  # not connected
  JP10 = Header 1 [package=1x01_offset]  # not connected
  JP11 = Header 1 [package=1x01_offset]
  JP12 = Header 1 [package=1x01_offset]  # not connected
  JP13 = Header 1 [package=1x01_offset]  # not connected
  JP14 = Header 1 [package=1x01_offset]  # not connected
  JP15 = Header 1 [package=1x01_offset]  # not connected
  JP16 = Header 1 [package=1x01_offset]  # not connected
  JP17 = Header 1 [package=1x01_offset]
  JP18 = Header 1 [package=1x01_offset]  # not connected
  JP19 = Header 1 [package=1x01_offset]  # not connected
  JP20 = Header 1 [package=1x01_offset]  # not connected
  JP21 = Header 1 [package=1x01_offset]  # not connected
  R9 = Resistor [tolerance=±5% resistance=10k package="0402 [SMD]"]  # not connected
  JP22 = Header 1 [package=1x01_offset]  # not connected
  JP23 = Header 1 [package=1x01_offset]  # not connected
  JP24 = Header 1 [package=1x01_offset]  # not connected
  JP25 = Header 1 [package=1x01_offset]  # not connected
  JP26 = Header 1 [package=1x01_offset]  # not connected
  JP27 = Header 1 [package=1x01_offset]  # not connected
  JP28 = Header 1 [package=1x01_offset]  # not connected
  JP29 = Header 1 [package=1x01_offset]  # not connected
  JP30 = Header 1 [package=1x01_offset]  # not connected
  JP31 = Header 1 [package=1x01_offset]  # not connected
  JP32 = Header 1 [package=1x01_offset]  # not connected
  JP33 = Header 1 [package=1x01_offset]  # not connected
  JP34 = Header 1 [package=1x01_offset]
  JP35 = Header 1 [package=1x01_offset]  # not connected
  MPU9250_MPU-1 = SparkFun IMU Breakout - MPU-9250 [part_number=" SEN-13762"]
  M1 = RioRand LM2596
  U2 = LIPO-1000mAh [package=lipo-1000]
  U3 = SWITCH_SPDT [package=kps-1290]
  TP1 = TP4056 [chip_label=TP4056 package="DIP (Dual Inline) [THT]"]

nets:
  N1: U1.3.3, MPU9250_MPU-1.VDD
  GND: U1.GND, MPU9250_MPU-1.GND, M1.Pin_4
  N2: U1.VIN, M1.Pin_3
  N3: U1.GPIO21, MPU9250_MPU-1.SDA/SDI
  N4: U1.GPIO22, MPU9250_MPU-1.SCL/SCLK
  N5: JP3.4, JP34.1
  N6: JP8.1, JP11.1, JP17.1
  N7: M1.Pin_1, U3.P
  N8: M1.Pin_2, TP1.pin6
  N9: U2.+, TP1.pin4
  N10: U2.-, TP1.pin5
  N11: U3.S, TP1.pin3

notes:
  ZNX-01 plug

custom parts:
  ESP32-38PinWide: Generic 38-Pin ESP32 with wide format (only access to one side of pins on a breadboard) based on Stephen Lilley's HiLetgo ESP-WROOM-32 ESP32 ESP-32S Development Board.
  TP4056: A DIP stand-in part for whatever IC you want. With 6 pins on a 300mil dual inline package (DIP) footprint.
